// Digital circuit instruction_mem.dig as structural Verilog
module instruction_mem (
  input  [31:0] address,
  output [31:0] instruction
);

  wire [31:0] div_1_q;

  Div #(.Bits(32)) div_1 (.a(address), .b(32'h4), .q(div_1_q));  // open: r
  ROM #(.AddrBits(8), .Bits(32)) rom_1 (.A(div_1_q[7:0]), .sel(1'b1), .D(instruction));

  // Notes on the sheet:
  //   contents of rom_1 (hex, n*v repeats v):
  //   20080001,20090028,ac080000,ac080004,200a0008,11490004,8d4bfffc,8d4cfff8,016cf820,ad5f0000,214a0004,
  //   08000005
endmodule
