// Digital circuit PC.dig as structural Verilog
module PC (
  input  Clok,
  input  [31:0] PC_IN,
  output [31:0] PC_OUT
);

  wire [31:0] d_ff_1_q;

  D_FF #(.Bits(32)) d_ff_1 (.D(PC_IN), .C(~Clok), .Q(d_ff_1_q));  // open: nQ
  D_FF #(.Bits(32)) d_ff_2 (.D(d_ff_1_q), .C(Clok), .Q(PC_OUT));  // open: nQ
endmodule
