// Digital circuit EX-MEM.dig as structural Verilog
module EX_MEM (
  input  [31:0] R_2,
  input  [31:0] Result,
  input  [4:0] Dest,
  input  Clk,
  input  MTR,
  input  MW,
  input  MR,
  input  RW,
  output [31:0] O_R2,
  output [31:0] O_Result,
  output [4:0] O_Dest,
  output O_MTR,
  output O_MW,
  output O_MR,
  output O_RW
);

  wire pulse_1_p;

  pulse pulse_1 (.Clk(Clk), .P(pulse_1_p));
  // reg reg_1: pin names not known; wires that end beside it: RW, Clk, pulse_1_p, O_RW
  // reg reg_2: pin names not known; wires that end beside it: MR, Clk, pulse_1_p, O_MR
  // reg reg_3: pin names not known; wires that end beside it: MW, Clk, pulse_1_p, O_MW
  // reg reg_4: pin names not known; wires that end beside it: MTR, Clk, pulse_1_p, O_MTR
  reg32 reg32_1 (.In(Result), .Clk(Clk), .Clr(pulse_1_p), .Out(O_Result));
  reg32 reg32_2 (.In(R_2), .Clk(Clk), .Clr(pulse_1_p), .Out(O_R2));
  reg5 reg5_1 (.In(Dest), .Clk(Clk), .Clr(pulse_1_p), .Out(O_Dest));

  // Notes on the sheet:
  //   R_2: Dado lido do registrador 2
  //   O_R2: Dado lido do registrador 2
  //   Result: Dado lido do registrador 1
  //   O_Result: Dado lido do registrador 1
  //   Dest: Sinal extendido
  //   O_Dest: Sinal extendido
  //   M
endmodule
