// Digital circuit ID-EX.dig as structural Verilog
module ID_EX (
  input  [31:0] R_2,
  input  [31:0] R_1,
  input  [31:0] S_32,
  input  Clk,
  input  MTR,
  input  MW,
  input  MR,
  input  RgD,
  input  AluS,
  input  [1:0] AO,
  input  RW,
  output [31:0] O_R2,
  output [31:0] O_R1,
  output [31:0] O_S32,
  output O_MTR,
  output O_MW,
  output O_MR,
  output O_RgD,
  output O_AluS,
  output [1:0] O_AO,
  output O_RW
);

  wire pulse_1_p;

  pulse pulse_1 (.Clk(Clk), .P(pulse_1_p));
  // reg reg_1: pin names not known; wires that end beside it: RW, Clk, pulse_1_p, O_RW
  // reg reg_2: pin names not known; wires that end beside it: MR, Clk, pulse_1_p, O_MR
  // reg reg_3: pin names not known; wires that end beside it: MW, Clk, pulse_1_p, O_MW
  // reg reg_4: pin names not known; wires that end beside it: MTR, Clk, pulse_1_p, O_MTR
  // reg reg_5: pin names not known; wires that end beside it: RgD, Clk, pulse_1_p, O_RgD
  // reg reg_6: pin names not known; wires that end beside it: AluS, Clk, pulse_1_p, O_AluS
  reg2 reg2_1 (.In(AO), .Clk(Clk), .Clr(pulse_1_p), .Out(O_AO));
  reg32 reg32_1 (.In(R_1), .Clk(Clk), .Clr(pulse_1_p), .Out(O_R1));
  reg32 reg32_2 (.In(R_2), .Clk(Clk), .Clr(pulse_1_p), .Out(O_R2));
  reg32 reg32_3 (.In(S_32), .Clk(Clk), .Clr(pulse_1_p), .Out(O_S32));

  // Notes on the sheet:
  //   R_2: Dado lido do registrador 2
  //   O_R2: Dado lido do registrador 2
  //   R_1: Dado lido do registrador 1
  //   O_R1: Dado lido do registrador 1
  //   S_32: Sinal extendido
  //   O_S32: Sinal extendido
  //   M
  //   EX
endmodule
