// Digital circuit ID-EX_part_2.dig as structural Verilog
module ID_EX_part_2 (
  input  Clk,
  input  [4:0] RgD_1,
  input  [4:0] RgD_2,
  output [4:0] O_RgD_1,
  output [4:0] O_RgD_2
);

  wire pulse_1_p;

  pulse pulse_1 (.Clk(Clk), .P(pulse_1_p));
  reg5 reg5_1 (.In(RgD_1), .Clk(Clk), .Clr(pulse_1_p), .Out(O_RgD_1));
  reg5 reg5_2 (.In(RgD_2), .Clk(Clk), .Clr(pulse_1_p), .Out(O_RgD_2));

  // Notes on the sheet:
  //   RgD_1: Dado lido do registrador 2
  //   O_RgD_1: Dado lido do registrador 2
  //   RgD_2: Sinal extendido
  //   O_RgD_2: Sinal extendido
endmodule
