// Digital circuit MEM-WB.dig as structural Verilog
module MEM_WB (
  input  [31:0] Alu_res,
  input  [31:0] Read_D,
  input  [4:0] Dest,
  input  Clk,
  input  MTR,
  input  RW,
  output [31:0] O_Alu_res,
  output [31:0] O_Read_D,
  output [4:0] O_Dest,
  output O_MTR,
  output O_RW
);

  wire pulse_1_p;

  pulse pulse_1 (.Clk(Clk), .P(pulse_1_p));
  // reg reg_1: pin names not known; wires that end beside it: RW, Clk, pulse_1_p, O_RW
  // reg reg_2: pin names not known; wires that end beside it: MTR, Clk, pulse_1_p, O_MTR
  reg32 reg32_1 (.In(Read_D), .Clk(Clk), .Clr(pulse_1_p), .Out(O_Read_D));
  reg32 reg32_2 (.In(Alu_res), .Clk(Clk), .Clr(pulse_1_p), .Out(O_Alu_res));
  reg5 reg5_1 (.In(Dest), .Clk(Clk), .Clr(pulse_1_p), .Out(O_Dest));

  // Notes on the sheet:
  //   Alu_res: Dado lido do registrador 2
  //   O_Alu_res: Dado lido do registrador 2
  //   Read_D: Dado lido da memória
  //   O_Read_D: Dado lido do registrador 1
  //   Dest: Sinal extendido
  //   O_Dest: Sinal extendido
endmodule
