// Digital circuit Stall.dig as structural Verilog
module Stall (
  input  ID_EX_MR,
  input  [4:0] ID_EX_Rt,
  input  [4:0] IF_ID_Rs,
  input  [4:0] IF_ID_Rt,
  output Stall
);

  wire comparator_1_eq, comparator_2_eq, or_1_out;

  and and_1 (Stall, or_1_out, ID_EX_MR);
  Comparator #(.Bits(5)) comparator_1 (.a(IF_ID_Rs), .b(ID_EX_Rt), .eq(comparator_1_eq));  // open: gt, lt
  or or_1 (or_1_out, comparator_2_eq, comparator_1_eq);
  Comparator #(.Bits(5)) comparator_2 (.a(IF_ID_Rt), .b(ID_EX_Rt), .eq(comparator_2_eq));  // open: gt, lt
endmodule
