// Digital circuit main.dig as structural Verilog
module main (
  input  [4:0] clock,
  input  pc_reset
);

  wire ALU_Control_p2, ALU_Control_p5, APC, Banco_de_registradores_p1, Banco_de_registradores_p7,
       Banco_de_registradores_p8, branch, ex_mem_1_mem_memread, ex_mem_1_mem_memtoreg, ex_mem_1_mem_memwrite,
       ex_mem_1_wb_regwrite, id_ex_1_p16, id_ex_1_p17, id_ex_1_p18, id_ex_1_p19, id_ex_1_p20, id_ex_1_p21,
       id_ex_1_p22, id_ex_1_p23, if_id_1_p2, mem_wb_1_wb_memtoreg, stall_1_id_stall, stall_1_if_stall, ULA_p5;
  wire [1:0] FA, FB;
  wire [4:0] ALU_Control_p1, Banco_de_registradores_p5, ex_mem_1_mem_dstaddr, multiplexer_4_out, undriven_2,
       undriven_3;
  wire [5:0] if_id_1_p4, if_id_1_p4_3;
  wire [8:0] multiplexer_3_out, UC_b;
  wire [25:6] if_id_1_p4_2;
  wire [31:0] add_1_s, add_2_s, barrelshifter_1_out, bitextender_1_out, Constant, ex_mem_1_mem_rtdata,
       id_ex_1_p24, Mem_result, mem_wb_1_wb_readdata, mem_wb_1_wb_result, \Memória_de_dados_data ,
       \Memória_de_instruções_instruction , multiplexer_2_out, multiplexer_5_out, multiplexer_6_out,
       multiplexer_7_out, pc_1_address, R31, ULA_p6, undriven, undriven_5, WB;
  wire [31:6] undriven_4;

  Multiplexer #(.Bits(32)) multiplexer_1 ();  // open: sel, in_0, in_1, out
  Add #(.Bits(32)) add_1 (.a(pc_1_address), .b(32'h4), .c_i(1'b0), .s(add_1_s));  // open: c_o
  BarrelShifter #(.Bits(32)) barrelshifter_1 (.in(Constant), .shift(6'b000010), .out(barrelshifter_1_out));
  PC pc_1 (.clock(clock[0]), .write(undriven_5), .reset(pc_reset), .enable(APC), .address(pc_1_address));
  Add #(.Bits(32)) add_2 (.a(add_1_s), .b(barrelshifter_1_out), .c_i(1'b0), .s(add_2_s));  // open: c_o
  instruction_mem \Memória_de_instruções  (.address(pc_1_address), .instruction(\Memória_de_instruções_instruction ));
  Multiplexer #(.Bits(32)) multiplexer_2 (
    .sel(stall_1_if_stall), .in_0(\Memória_de_instruções_instruction ), .in_1({undriven_4, 6'b000010}),
    .out(multiplexer_2_out));
  // IF_ID if_id_1: pin names not known; wires that end beside it: multiplexer_2_out, if_id_1_p2, clock, {if_id_1_p4_3, if_id_1_p4_2[25:21], clock, if_id_1_p4_2[15:6], if_id_1_p4}
  not not_1 (if_id_1_p2, stall_1_id_stall);
  Control UC (
    .RgD(UC_b[0]), .AluS(UC_b[1]), .MTR(UC_b[2]), .RW(UC_b[3]), .MR(UC_b[4]), .MW(UC_b[5]), .B(UC_b[6]),
    .AO_1(UC_b[7]), .AO_0(UC_b[8]), .APC(APC), .Op(if_id_1_p4_3));  // open: J
  // _32x32 Banco_de_registradores: pin names not known; wires that end beside it: Banco_de_registradores_p1, WB, if_id_1_p4_2[25:21], clock, Banco_de_registradores_p5, clock, Banco_de_registradores_p7, Banco_de_registradores_p8, R31
  BitExtender #(.inputBits(16), .outputBits(32)) bitextender_1 (
    .in({if_id_1_p4_2[15:6], if_id_1_p4}), .out(bitextender_1_out));
  Seven_Seg_Hex seven_seg_hex_1 (.d(R31[19:16]), .dp(1'b0));
  Multiplexer #(.Bits(9)) multiplexer_3 (
    .sel(stall_1_id_stall), .in_0(UC_b), .in_1({9{1'b0}}), .out(multiplexer_3_out));
  Seven_Seg_Hex seven_seg_hex_2 (.d(R31[15:12]), .dp(1'b0));
  Stall stall_1 (
    .IF_ID_rs(if_id_1_p4_2[25:21]), .IF_ID_rt(clock), .ID_EX_memRead(id_ex_1_p18), .ID_EX_rt(undriven_3),
    .branch(branch), .ID_stall(stall_1_id_stall), .IF_stall(stall_1_if_stall));
  Seven_Seg_Hex seven_seg_hex_3 (.d(R31[11:8]), .dp(1'b0));
  // ID_EX id_ex_1: pin names not known; wires that end beside it: multiplexer_3_out[3], multiplexer_3_out[2], multiplexer_3_out[4], multiplexer_3_out[5], multiplexer_3_out[6], multiplexer_3_out[0], multiplexer_3_out[1], multiplexer_3_out[8:7], Banco_de_registradores_p7, Banco_de_registradores_p8, bitextender_1_out, if_id_1_p4_2[25:21], clock, if_id_1_p4_2[15:11], if_id_1_p4, id_ex_1_p16, id_ex_1_p17, id_ex_1_p18, id_ex_1_p19, id_ex_1_p20, id_ex_1_p21, id_ex_1_p22, id_ex_1_p23, id_ex_1_p24
  Seven_Seg_Hex seven_seg_hex_4 (.d(R31[7:4]), .dp(1'b0));
  Seven_Seg_Hex seven_seg_hex_5 (.d(R31[3:0]), .dp(1'b0));
  Multiplexer #(.Bits(5)) multiplexer_4 (
    .sel(id_ex_1_p21), .in_0(undriven_3), .in_1(ALU_Control_p1), .out(multiplexer_4_out));
  Multiplexer #(.Selector_Bits(2), .Bits(32)) multiplexer_5 (
    .sel(FB), .in_0(undriven), .in_1(WB), .in_2(Mem_result), .in_3(Mem_result), .out(multiplexer_5_out));
  // ALU_Control ALU_Control: pin names not known; wires that end beside it: ALU_Control_p1, ALU_Control_p2, id_ex_1_p23, ALU_Control_p2, ALU_Control_p5
  Multiplexer #(.Bits(32)) multiplexer_6 (
    .sel(id_ex_1_p22), .in_0(multiplexer_5_out), .in_1(Constant), .out(multiplexer_6_out));
  Multiplexer #(.Selector_Bits(2), .Bits(32)) multiplexer_7 (
    .sel(FA), .in_0(id_ex_1_p24), .in_1(WB), .in_2(Mem_result), .in_3(Mem_result), .out(multiplexer_7_out));
  // ula ULA: pin names not known; wires that end beside it: ALU_Control_p5, multiplexer_7_out, multiplexer_6_out, {6{1'b0}}, ULA_p5, ULA_p6
  forwarding_unit Unidade_de_forwarding (
    .RS(undriven_2), .RT(undriven_3), .EX_MEM_dest(ex_mem_1_mem_dstaddr),
    .MEM_WB_dest(Banco_de_registradores_p5), .EX_MEM_rw(ex_mem_1_wb_regwrite),
    .MEM_WB_rw(Banco_de_registradores_p1), .FA(FA), .FB(FB));
  and and_1 (branch, id_ex_1_p20, ULA_p5);
  EX_MEM ex_mem_1 (
    .EX_regWrite(id_ex_1_p16), .EX_memRead(id_ex_1_p18), .EX_memWrite(id_ex_1_p19),
    .EX_memToReg(id_ex_1_p17), .EX_result(ULA_p6), .EX_rtData(multiplexer_5_out),
    .EX_dstAddr(multiplexer_4_out), .clock(clock[0]), .WB_regWrite(ex_mem_1_wb_regwrite),
    .MEM_memRead(ex_mem_1_mem_memread), .MEM_memWrite(ex_mem_1_mem_memwrite),
    .MEM_memToReg(ex_mem_1_mem_memtoreg), .MEM_result(Mem_result), .MEM_rtData(ex_mem_1_mem_rtdata),
    .MEM_dstAddr(ex_mem_1_mem_dstaddr));
  memory_24x32 \Memória_de_dados  (
    .address(Mem_result[23:0]), .write_data(ex_mem_1_mem_rtdata), .mem_write(ex_mem_1_mem_memwrite),
    .mem_read(ex_mem_1_mem_memread), .clock(clock[0]), .data(\Memória_de_dados_data ));
  MEM_WB mem_wb_1 (
    .MEM_regWrite(ex_mem_1_wb_regwrite), .MEM_memToReg(ex_mem_1_mem_memtoreg),
    .MEM_readData(\Memória_de_dados_data ), .MEM_result(Mem_result), .MEM_dstAddr(ex_mem_1_mem_dstaddr),
    .clock(clock[0]), .WB_regWrite(Banco_de_registradores_p1), .WB_memToReg(mem_wb_1_wb_memtoreg),
    .WB_readData(mem_wb_1_wb_readdata), .WB_result(mem_wb_1_wb_result), .WB_dstAddr(Banco_de_registradores_p5));
  Multiplexer #(.Bits(32)) multiplexer_8 (
    .sel(mem_wb_1_wb_memtoreg), .in_0(mem_wb_1_wb_result), .in_1(mem_wb_1_wb_readdata), .out(WB));
  // Pins of 1 and 5 bits meet at clock
  // Pins of 6 and 32 bits meet at {undriven_4, 6'b000010}
  // also tied to GND on the sheet: {add_1_s[1], add_1_s[2], add_1_s[3], add_1_s[4], add_1_s[5], add_1_s[6], add_1_s[7], add_1_s[8], add_1_s[9], add_1_s[10], add_1_s[11], add_1_s[12], add_1_s[13], add_1_s[14], add_1_s[15], add_1_s[16], add_1_s[17], add_1_s[18], add_1_s[19], add_1_s[20], add_1_s[21], add_1_s[22], add_1_s[23], add_1_s[24], add_1_s[25], add_1_s[26], add_1_s[27], add_1_s[28], add_1_s[29], add_1_s[30], add_1_s[31]}
  // also tied to VCC on the sheet: add_1_s[0]

  // Notes on the sheet:
  //   clock: Hz: 10
  //   main:
  //       li $ra, 10
  //   loop:
  //       beq $ra, $zero, done
  //       addi $ra, $ra, -1
  //       beq $zero, $zero, loop
  //   done:
  //   Reg Destino
  //   MEM/WB_Dest
  //   MEM/WB_RegWrite
endmodule
